# Fritzing sketch home-assistant-temperature-monitor (saved by Fritzing 0.9.3b)

parts:
  Part1 = Adafruit Perma-Proto HAT [part_number="Adafruit #2314 and #2310"]
  Raspberry_Pi_Zero1 = Raspberry Pi Zero
  LCD1 = Adafruit Negative RGB 2x16 LCD
  S2 = Pushbutton [package="[THT]"]
  LED1 = LED - 5mm [color="Red (633nm)" package="5 mm [THT]"]
  R1 = Resistor [tolerance=±5% resistance=220 package="0402 [SMD]"]
  R2 = Resistor [tolerance=±5% resistance=220 package="2512 [SMD]"]
  Part2 = Adafruit Si7021 Temp Humidity [part_number="Adafruit #3251"]
  U3 = POT [package=alps_pot]

nets:
  N1: Part1.SDA, Raspberry_Pi_Zero1.GPIO2, Part2.SDA
  N2: Part1.SCL, Raspberry_Pi_Zero1.GPIO3, Part2.SCL
  N3: Part1.GPIO4, Raspberry_Pi_Zero1.GPIO4, LCD1.no_name_yet#15
  N4: Part1.GPIO17, Raspberry_Pi_Zero1.GPIO17, LCD1.no_name_yet#16
  N5: Part1.GPIO18, Raspberry_Pi_Zero1.GPIO18, LCD1.no_name_yet#13
  N6: Part1.GPIO27, Raspberry_Pi_Zero1.GPIO27, LCD1.no_name_yet#3
  N7: Part1.GPIO22, Raspberry_Pi_Zero1.GPIO22, LCD1.no_name_yet#5
  N8: Part1.GPIO23, Raspberry_Pi_Zero1.GPIO23, LCD1.no_name_yet#12
  N9: Part1.GPIO24, Raspberry_Pi_Zero1.GPIO24, LCD1.no_name_yet#11
  N10: Part1.GPIO25, Raspberry_Pi_Zero1.GPIO25, LCD1.no_name_yet#10
  N11: Part1.SPI_CE1, Raspberry_Pi_Zero1.GPIO7, LCD1.no_name_yet#17
  N12: Part1.GPIO19, Part1.N$20#247, Raspberry_Pi_Zero1.GPIO19
  3V3: Part1.3.3V, Raspberry_Pi_Zero1.3v3, Raspberry_Pi_Zero1.3V3, LED1.anode
  5V: Part1.5.0V, Raspberry_Pi_Zero1.5V, LCD1.no_name_yet#1, LCD1.no_name_yet#14, R2.Pin_1, Part2.VIN, U3.A
  GND: Part1.GND, Raspberry_Pi_Zero1.GND, LCD1.no_name_yet#0, LCD1.no_name_yet#4, S2.Pin_3, S2.Pin_4, R1.Pin_0, Part2.GND, U3.E
  N13: Part1.TXD, Raspberry_Pi_Zero1.GPIO14
  N14: Part1.RXD, Raspberry_Pi_Zero1.GPIO15
  N15: Part1.SPI_MOSI, Raspberry_Pi_Zero1.GPIO10
  N16: Part1.SPI_MISO, Raspberry_Pi_Zero1.GPIO9
  N17: Part1.SPI_SCLK, Raspberry_Pi_Zero1.GPIO11
  N18: Part1.SPI_CE0, Raspberry_Pi_Zero1.GPIO8
  N19: Part1.EEDATA, Raspberry_Pi_Zero1.ID_SD
  N20: Part1.EECLK, Raspberry_Pi_Zero1.ID_SC
  N21: Part1.GPIO5, Raspberry_Pi_Zero1.GPIO5
  N22: Part1.GPIO6, Raspberry_Pi_Zero1.GPIO6
  N23: Part1.GPIO12, Raspberry_Pi_Zero1.GPIO12
  N24: Part1.GPIO13, Raspberry_Pi_Zero1.GPIO13
  N25: Part1.GPIO16, Raspberry_Pi_Zero1.GPIO16
  N26: Part1.GPIO26, Raspberry_Pi_Zero1.GPIO26
  N27: Part1.GPIO20, Raspberry_Pi_Zero1.GPIO20
  N28: Part1.GPIO21, Raspberry_Pi_Zero1.GPIO21
  N29: Part1.N$20#246, S2.Pin_1
  N30: Part1.N$20#248, R2.Pin_0
  N31: LCD1.no_name_yet#2, U3.S
  N32: LED1.cathode, R1.Pin_1

custom parts:
  Adafruit Perma-Proto HAT: To kick off the Adafruit HAT party, we have this Perma-Proto inspired plug in daughter board. It has a grid of 0.1" prototyping soldering holes for attaching chips, resistors, LED, potentiometers and more. The holes are connected underneath with traces to mimic the solderless breadboards you're familiar. There's also long power strips for +3V, +5V and Ground connections to the Pi. Near the top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
  Adafruit Negative RGB 2x16 LCD: Adafruit Negative 2x16 LCD Display with RGB Backlight
  Adafruit Si7021 Temp Humidity: It's summer and you're sweating and your hair's all frizzy and all you really want to know is why the weatherman said this morning that today's relative humidity would max out at a perfectly reasonable 42% when it feels more like 77%. Enter the Si7021 Temperature + Humidity Sensor - the best way to prove the weatherman wrong! This lovely sensor for Silicon labs has ± 3% relative humidity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
